# Fritzing sketch my_clock (saved by Fritzing 0.9.6b)
breadboards: 1

parts:
  Raspberry_Pi_1 = Raspberry Pi 3 [part_number=RPI-3-V1.2]
  R8 = Resistor [tolerance=±5% resistance=100 package="2010 [SMD]"]
  7_Segment_4_Digit_Display2 = 7-SEGMENT-4DIGIT common anode [part_number="5461BS - 5462BS" package=7-segment-4digit-anode]
  R9 = Resistor [tolerance=±5% resistance=100 package="2010 [SMD]"]
  R10 = Resistor [tolerance=±5% resistance=100 package="2010 [SMD]"]
  R11 = Resistor [tolerance=±5% resistance=100 package="2010 [SMD]"]

nets:
  N1: Raspberry_Pi_1.GPIO2, 7_Segment_4_Digit_Display2.pin_7
  N2: Raspberry_Pi_1.GPIO3, 7_Segment_4_Digit_Display2.pin_4
  N3: Raspberry_Pi_1.GPIO4, 7_Segment_4_Digit_Display2.pin_3
  N4: Raspberry_Pi_1.GPIO10, R11.Pin_1
  N5: Raspberry_Pi_1.GPIO9, 7_Segment_4_Digit_Display2.pin_11
  N6: Raspberry_Pi_1.GPIO11, R10.Pin_1
  N7: Raspberry_Pi_1.GPIO5, 7_Segment_4_Digit_Display2.pin_2
  N8: Raspberry_Pi_1.GPIO6, 7_Segment_4_Digit_Display2.pin_1
  N9: Raspberry_Pi_1.GPIO13, R8.Pin_1
  N10: Raspberry_Pi_1.GPIO12, R9.Pin_1
  N11: Raspberry_Pi_1.GPIO7, 7_Segment_4_Digit_Display2.pin_5
  N12: Raspberry_Pi_1.GPIO8, 7_Segment_4_Digit_Display2.pin_10
  N13: R8.Pin_0, 7_Segment_4_Digit_Display2.pin_6
  N14: 7_Segment_4_Digit_Display2.pin_8, R9.Pin_0
  N15: 7_Segment_4_Digit_Display2.pin_9, R10.Pin_0
  N16: 7_Segment_4_Digit_Display2.pin_12, R11.Pin_0

custom parts:
  7-SEGMENT-4DIGIT common anode: A 7 Segment 4 Digit common anode display, with decimal points
